# Fritzing sketch two_osc_touch_w_pitch (saved by Fritzing 0.9.4)
breadboards: 1

parts:
  Teensy_3_1 = Teensy 3.1
  TRS1 = Audio Jack (TRS) 3.5mm [package="PG203J [THT]"]
  R2 = Rotary Potentiometer (Small) [maximum_resistance=100kΩ package=THT]
  R3 = Rotary Potentiometer (Small) [maximum_resistance=100kΩ package=THT]

nets:
  N1: Teensy_3_1.GND, TRS1.Sleeve, R2.leg2, R3.leg2
  N2: Teensy_3_1.A14/DAC, TRS1.Tip
  N3: Teensy_3_1.Vin, R2.leg1, R3.leg1
