# Fritzing sketch two_osc_touch (saved by Fritzing 0.9.4)
breadboards: 1

parts:
  Teensy_3_1 = Teensy 3.1
  TRS1 = Audio Jack (TRS) 3.5mm [package="PG203J [THT]"]

nets:
  N1: Teensy_3_1.GND, TRS1.Sleeve
  N2: Teensy_3_1.A14/DAC, TRS1.Tip
